# Fritzing sketch Cardio Freq (saved by Fritzing 0.9.3b)
breadboards: 1

parts:
  Composant1 = Arduino Uno (Rev3) - ICSP
  IC1 = IC, DIP package, 14 pins [chip_label=IC]
  LED1 = LED - 5mm [color="Red (633nm)" package="5 mm [THT]"]
  R1 = Resistor [tolerance=±5% resistance=100 package=THT]
  R2 = Resistor [tolerance=±5% resistance=470k package=THT]
  C1 = Electrolytic Capacitor [capacitance=100nF package="100 mil [THT, electrolytic]"]
  R3 = Resistor [tolerance=±5% resistance=1k package=THT]
  R4 = Resistor [tolerance=±5% resistance=68k package=THT]
  C2 = Electrolytic Capacitor [capacitance=1µF package="100 mil [THT, electrolytic]"]
  R5 = Resistor [tolerance=±5% resistance=22k package=THT]
  R6 = Resistor [tolerance=±5% resistance=2.2k package=THT]
  LED2 = LED - 5mm [color="Infrared (940nm)" package="5 mm [THT]"]
  LED3 = LED - 5mm [color="Blue (430nm)" package="5 mm [THT]"]

nets:
  N1: Composant1.A0, LED1.cathode, R1.Pin_1
  N2: Composant1.5V, IC1.pin4, R5.Pin_1, R6.Pin_1
  N3: Composant1.GND, IC1.pin11, LED1.anode, R3.Pin_0, R4.Pin_0, LED2.cathode, LED3.anode
  N4: IC1.pin5, R4.Pin_1, C2.-
  N5: IC1.pin6, R2.Pin_0, C1.+, R3.Pin_1
  N6: IC1.pin7, R1.Pin_0, R2.Pin_1, C1.-
  N7: C2.+, R5.Pin_0, LED3.cathode
  N8: R6.Pin_0, LED2.anode
