# Fritzing sketch Preshot Cardio Freq (saved by Fritzing 0.9.3b)
breadboards: 1

parts:
  Composant1 = Arduino Uno (Rev3) - ICSP
  IC1 = IC, DIP package, 14 pins [chip_label=IC]
  R1 = Resistor [tolerance=±5% resistance=2.2k package="2512 [SMD]"]
  LED1 = smd LED [color="Blue (430nm)" package="0805 [SMD]"]
  R2 = Resistor [tolerance=±5% resistance=22k package="2010 [SMD]"]
  C1 = Electrolytic Capacitor [capacitance=1µF package="100 mil [THT, electrolytic]"]
  R4 = Resistor [tolerance=±5% resistance=68k package="2512 [SMD]"]
  R5 = Resistor [tolerance=±5% resistance=1k package="2512 [SMD]"]
  C2 = Electrolytic Capacitor [capacitance=100nF package="100 mil [THT, electrolytic]"]
  R6 = Resistor [tolerance=±5% resistance=470k package=THT]
  R7 = Resistor [tolerance=±5% resistance=100 package=THT]
  LED2 = smd LED [color="Red (633nm)" package="0805 [SMD]"]
  LED4 = smd LED [color="Infrared (940nm)" package="0805 [SMD]"]

nets:
  N1: Composant1.A0, R7.Pin_1, LED2.anode
  N2: Composant1.GND, IC1.pin11, LED1.cathode, R4.Pin_0, R5.Pin_1, LED2.cathode, LED4.cathode
  N3: Composant1.5V, IC1.pin4, R1.Pin_0, R2.Pin_0
  N4: IC1.pin5, C1.+, R4.Pin_1
  N5: IC1.pin6, R5.Pin_0, C2.-, R6.Pin_0
  N6: IC1.pin7, C2.+, R6.Pin_1, R7.Pin_0
  N7: R1.Pin_1, LED1.anode
  N8: R2.Pin_1, C1.-, LED4.anode
