# Fritzing sketch Schéma Elec Complet (saved by Fritzing 0.9.3b)
breadboards: 3

parts:
  Composant1 = Arduino Mega ADK (Rev3)
  IC1 = IC, DIP package, 14 pins [chip_label=IC]
  R1 = Resistor [tolerance=±5% resistance=22k package=THT]
  R2 = Resistor [tolerance=±5% resistance=2.2k package=THT]
  LED1 = LED - 5mm [color="Blue (430nm)" package="5 mm [THT]"]
  LED2 = LED - 5mm [color="Infrared (940nm)" package="5 mm [THT]"]
  C1 = Electrolytic Capacitor [capacitance=1µF package="100 mil [THT, electrolytic]"]
  R3 = Resistor [tolerance=±5% resistance=68k package=THT]
  R4 = Resistor [tolerance=±5% resistance=1k package=THT]
  C2 = Electrolytic Capacitor [capacitance=100nF package="100 mil [THT, electrolytic]"]
  R5 = Resistor [tolerance=±5% resistance=470k package=THT]
  R6 = Resistor [tolerance=±5% resistance=100 package=THT]
  LED3 = LED - 5mm [color="Red (633nm)" package="5 mm [THT]"]
  R7 = Resistor [tolerance=±5% resistance=220 package=THT]
  LED4 = LED - 5mm [color="Red (633nm)" package="5 mm [THT]"]
  LED5 = LED - 5mm [color="Red (633nm)" package="5 mm [THT]"]
  LED6 = LED - 5mm [color="Red (633nm)" package="5 mm [THT]"]
  LED7 = LED - 5mm [color="Red (633nm)" package="5 mm [THT]"]
  LED8 = LED - 5mm [color="Red (633nm)" package="5 mm [THT]"]
  LED9 = LED - 5mm [color="Red (633nm)" package="5 mm [THT]"]
  LED10 = LED - 5mm [color="Red (633nm)" package="5 mm [THT]"]
  LED11 = LED - 5mm [color="Red (633nm)" package="5 mm [THT]"]
  LED12 = LED - 5mm [color="Red (633nm)" package="5 mm [THT]"]
  LED13 = LED - 5mm [color="Red (633nm)" package="5 mm [THT]"]
  R8 = Resistor [tolerance=±5% resistance=220 package=THT]
  R9 = Resistor [tolerance=±5% resistance=220 package=THT]
  R10 = Resistor [tolerance=±5% resistance=220 package=THT]
  R11 = Resistor [tolerance=±5% resistance=220 package=THT]
  R12 = Resistor [tolerance=±5% resistance=220 package=THT]
  R13 = Resistor [tolerance=±5% resistance=220 package=THT]
  R14 = Resistor [tolerance=±5% resistance=220 package=THT]
  R15 = Resistor [tolerance=±5% resistance=220 package=THT]
  R16 = Resistor [tolerance=±5% resistance=220 package=THT]

nets:
  N1: Composant1.A0, R6.Pin_0, LED3.anode
  N2: Composant1.GND, IC1.pin4, LED1.cathode, LED2.anode, R3.Pin_0, R4.Pin_1, LED3.cathode, LED4.cathode, LED5.cathode, LED6.cathode, LED7.cathode, LED8.cathode, LED9.cathode, LED10.cathode, LED11.cathode, LED12.cathode, LED13.cathode
  N3: Composant1.D11_PWM, R7.Pin_0
  N4: Composant1.D10_PWM, R8.Pin_0
  N5: Composant1.D9_PWM, R9.Pin_0
  N6: Composant1.D8_PWM, R10.Pin_0
  N7: Composant1.5V, IC1.pin11, R1.Pin_1, R2.Pin_1
  N8: Composant1.D2_PWM, R16.Pin_0
  N9: Composant1.D3_PWM, R15.Pin_0
  N10: Composant1.D4_PWM, R14.Pin_0
  N11: Composant1.D5_PWM, R13.Pin_0
  N12: Composant1.D6_PWM, R12.Pin_0
  N13: Composant1.D7_PWM, R11.Pin_0
  N14: IC1.pin12, C1.+, R3.Pin_1
  N15: IC1.pin13, R4.Pin_0, C2.+, R5.Pin_0
  N16: IC1.pin14, C2.-, R5.Pin_1, R6.Pin_1
  N17: R1.Pin_0, LED2.cathode, C1.-
  N18: R2.Pin_0, LED1.anode
  N19: R7.Pin_1, LED13.anode
  N20: LED4.anode, R16.Pin_1
  N21: LED5.anode, R15.Pin_1
  N22: LED6.anode, R14.Pin_1
  N23: LED7.anode, R13.Pin_1
  N24: LED8.anode, R12.Pin_1
  N25: LED9.anode, R11.Pin_1
  N26: LED10.anode, R10.Pin_1
  N27: LED11.anode, R9.Pin_1
  N28: LED12.anode, R8.Pin_1
